// Logisim project questao4.circ as structural Verilog: 2 circuits, main circuit main
module main (
  input  \input ,
  output out_2
);

  wire clock_1_out, d_ff_1_q, d_ff_2_q, d_ff_3_q, state_manager_1_out_5, state_manager_1_out_6,
       state_manager_1_out_7;

  Clock clock_1 (.out(clock_1_out));
  State_Manager state_manager_1 (
    .\input (\input ), .state_bit2(d_ff_2_q), .state_bit1(d_ff_3_q), .state_bit0(d_ff_1_q),
    .out_5(state_manager_1_out_5), .out_6(state_manager_1_out_6), .out_7(state_manager_1_out_7));
  D_Flip_Flop d_ff_1 (.clk(clock_1_out), .D(state_manager_1_out_7), .Q(d_ff_1_q));  // open: Qn, preset, en, reset
  D_Flip_Flop d_ff_2 (.clk(clock_1_out), .D(state_manager_1_out_5), .Q(d_ff_2_q));  // open: Qn, preset, en, reset
  D_Flip_Flop d_ff_3 (.clk(clock_1_out), .D(state_manager_1_out_6), .Q(d_ff_3_q));  // open: Qn, preset, en, reset
  and and_1 (out_2, \input , d_ff_3_q, d_ff_2_q);
endmodule

module State_Manager (
  input  \input ,
  input  state_bit2,
  input  state_bit1,
  input  state_bit0,
  output out_5,
  output out_6,
  output out_7
);

  wire not_1_out, not_2_out, not_3_out, not_4_out, not_5_out;

  not not_1 (not_1_out, \input );
  not not_2 (not_2_out, state_bit2);
  not not_3 (not_3_out, state_bit2);
  not not_4 (not_4_out, state_bit1);
  not not_5 (not_5_out, state_bit1);
  and and_1 (out_5, not_1_out, not_2_out);
  and and_2 (out_6, not_3_out, not_4_out, state_bit0);
  and and_3 (out_7, \input , not_5_out);
endmodule
