// Logisim project questao6.circ as structural Verilog: 1 circuit, main circuit main
module main (
  input  Clock,
  input  Input,
  output out_3
);

  wire d_ff_1_q, d_ff_2_q, d_ff_3_q, d_ff_4_q, d_ff_5_q, not_1_out, not_2_out;

  D_Flip_Flop d_ff_1 (.clk(Clock), .D(Input), .Q(d_ff_1_q));  // open: Qn, preset, en, reset
  D_Flip_Flop d_ff_2 (.clk(Clock), .D(d_ff_1_q), .Q(d_ff_2_q));  // open: Qn, preset, en, reset
  D_Flip_Flop d_ff_3 (.clk(Clock), .D(d_ff_2_q), .Q(d_ff_3_q));  // open: Qn, preset, en, reset
  D_Flip_Flop d_ff_4 (.clk(Clock), .D(d_ff_3_q), .Q(d_ff_4_q));  // open: Qn, preset, en, reset
  D_Flip_Flop d_ff_5 (.clk(Clock), .D(d_ff_4_q), .Q(d_ff_5_q));  // open: Qn, preset, en, reset
  not not_1 (not_1_out, d_ff_3_q);
  not not_2 (not_2_out, d_ff_5_q);
  and and_1 (out_3, not_2_out, d_ff_4_q, not_1_out, d_ff_2_q);
endmodule
