// Logisim project Disjunção com nand.circ as structural Verilog: 8 circuits, main circuit Disjunção com nand
module Nand (
  input  x,
  input  y,
  output s
);

  wire and_out;

  and \and  (and_out, x, y);
  not \not  (s, and_out);
endmodule

module Nor (
  input  x,
  input  y,
  output s
);

  wire or_out;

  or \or  (or_out, x, y);
  not \not  (s, or_out);
endmodule

module \Disjunção_com_nand  (
  input  a,
  input  b,
  output s
);

  wire nand_2_out, nand_3_out, nand_out, not_1_out, not_2_out;

  and \nand  (nand_out, a, a);
  not not_1 (not_1_out, nand_out);
  not not_2 (not_2_out, nand_2_out);
  and nand_2 (nand_2_out, b, b);
  not not_3 (s, nand_3_out);
  and nand_3 (nand_3_out, not_1_out, not_2_out);
endmodule

module \Conjunção_com_nor  (
  input  a,
  input  b,
  output out_3
);

  wire Nor_2_s, Nor_s;

  Nor Nor (.x(a), .y(a), .s(Nor_s));
  Nor Nor_2 (.x(b), .y(b), .s(Nor_2_s));
  Nor Nor_3 (.x(Nor_s), .y(Nor_2_s), .s(out_3));
endmodule

module \Conjunção_com_nand  (
  input  a,
  input  b,
  output s
);

  wire nand_s;

  Nand \nand  (.x(a), .y(b), .s(nand_s));
  Nand nand_2 (.x(nand_s), .y(nand_s), .s(s));
endmodule

module \Disjunçaõ_com_nor  (
  input  in_1,
  input  in_2,
  output out_3
);

  wire nor_s;

  Nor \nor  (.x(in_1), .y(in_2), .s(nor_s));
  Nor nor_2 (.x(nor_s), .y(nor_s), .s(out_3));
endmodule

module Xor_com_nand (
  input  a,
  input  b,
  output s
);

  wire and_2_s, and_s, not_2_s, not_s;

  Nand \not  (.x(a), .y(a), .s(not_s));
  Nand not_2 (.x(b), .y(b), .s(not_2_s));
  \Conjunção_com_nand  \and  (.a(not_s), .b(b), .s(and_s));
  \Conjunção_com_nand  and_2 (.a(not_2_s), .b(a), .s(and_2_s));
  \Disjunção_com_nand  \or  (.a(and_s), .b(and_2_s), .s(s));

  // Notes on the sheet:
  //   Tudo utilizando apenas nand
endmodule

module xnor_com_nor (
  input  a,
  input  b,
  output out_3
);

  wire and_2_out_3, and_out_3, not_2_s, not_s, or_out_3;

  Nand \not  (.x(a), .y(a), .s(not_s));
  Nand not_2 (.x(b), .y(b), .s(not_2_s));
  \Conjunção_com_nor  \and  (.a(not_s), .b(b), .out_3(and_out_3));
  \Disjunçaõ_com_nor  \or  (.in_1(and_out_3), .in_2(and_2_out_3), .out_3(or_out_3));
  \Conjunção_com_nor  and_2 (.a(a), .b(not_2_s), .out_3(and_2_out_3));
  Nor not_3 (.x(or_out_3), .y(or_out_3), .s(out_3));

  // Notes on the sheet:
  //   Tudo usando portas e
  //   módulos com nor
endmodule
