// Logisim project Questao10.circ as structural Verilog: 1 circuit, main circuit main
module main (
  input  x,
  input  y,
  input  w,
  input  z,
  input  x_2,
  input  y_2,
  input  w_2,
  input  z_2,
  input  in_9,
  output out_10,
  output out_11
);

  wire and_1_out, and_2_out, and_3_out, and_4_out, not_1_out, not_2_out, not_3_out, not_4_out, not_5_out,
       not_6_out, not_7_out, not_8_out, not_9_out, not_10_out, or_1_out, or_3_out, or_4_out;

  not not_1 (not_1_out, y);
  not not_2 (not_2_out, w);
  not not_3 (not_3_out, z);
  or or_1 (or_1_out, not_1_out, not_2_out, not_3_out);
  and and_1 (and_1_out, x, or_1_out);
  or or_2 (out_10, in_9, and_1_out);
  not not_4 (not_4_out, y_2);
  not not_5 (not_5_out, x_2);
  not not_6 (not_6_out, w_2);
  and and_2 (and_2_out, z_2, w_2, y_2);
  not not_7 (not_7_out, x_2);
  or or_3 (or_3_out, not_4_out, w_2, not_5_out);
  not not_8 (not_8_out, or_3_out);
  and and_3 (and_3_out, y_2, not_6_out, x_2);
  not not_9 (not_9_out, and_3_out);
  or or_4 (or_4_out, and_2_out, not_7_out);
  buf and_4 (and_4_out, not_8_out);  // AND_Gate
  not not_10 (not_10_out, or_4_out);
  or or_5 (out_11, and_4_out, not_10_out);

  // Notes on the sheet:
  //   Circuito simplificado
  //   Circuito do Guia
endmodule
