// Logisim project Questao9.circ as structural Verilog: 1 circuit, main circuit main
module main (
  input  x,
  input  y,
  input  z,
  input  x_2,
  input  y_2,
  input  z_2,
  input  in_7,
  output out_8,
  output out_9
);

  wire and_1_out, and_2_out, and_3_out, and_4_out, not_1_out, not_2_out, not_3_out, not_4_out, not_5_out,
       not_6_out, not_7_out, not_8_out, or_1_out, or_3_out, or_4_out;

  not not_1 (not_1_out, z_2);
  not not_2 (not_2_out, y_2);
  or or_1 (or_1_out, not_1_out, not_2_out);
  and and_1 (and_1_out, x_2, or_1_out);
  or or_2 (out_8, in_7, and_1_out);
  not not_3 (not_3_out, y);
  not not_4 (not_4_out, x);
  or or_3 (or_3_out, not_3_out, not_4_out);
  and and_2 (and_2_out, y, x);
  and and_3 (and_3_out, z, y);
  not not_5 (not_5_out, x);
  not not_6 (not_6_out, or_3_out);
  not not_7 (not_7_out, and_2_out);
  or or_4 (or_4_out, and_3_out, not_5_out);
  and and_4 (and_4_out, not_6_out, not_7_out);
  not not_8 (not_8_out, or_4_out);
  or or_5 (out_9, and_4_out, not_8_out);

  // Notes on the sheet:
  //   Circuito simplificado
  //   Desenho do Guia
endmodule
