// Logisim project ULA.circ as structural Verilog: 8 circuits, main circuit Mux 2x1
module Mux_2x1 (
  input  E0,
  input  E1,
  input  escolha,
  output S
);

  wire And_2_out, And_out, Not_out;

  and And (And_out, E0, Not_out);
  not Not (Not_out, escolha);
  and And_2 (And_2_out, E1, escolha);
  or Or (S, And_out, And_2_out);
endmodule

module And_e_Nand_Paralelas (
  input  E0,
  input  E1,
  output S1,
  output S0
);

  and And (S1, E0, E1);
  nand Nand (S0, E0, E1);
endmodule

module Nor_e_Or_com_Mux (
  input  E0,
  input  E1,
  input  Selector,
  output S
);

  wire Nor_out, Or_out;

  nor Nor (Nor_out, E0, E1);
  or Or (Or_out, E0, E1);
  Mux_2x1 MUX (.E0(Nor_out), .E1(Or_out), .escolha(Selector), .S(S));
endmodule

module And_Nand_Or_Nor_com_Mux (
  input  E0,
  input  E1,
  input  Sel_1,
  input  Sel_0,
  output S
);

  wire And_out, MUX1_s, MUX2_s, NAND_out, nor_1_out, Or_out;

  nor nor_1 (nor_1_out, E1, E0);
  or Or (Or_out, E1, E0);
  not NAND (NAND_out, nor_1_out);
  not And (And_out, Or_out);
  Mux_2x1 MUX1 (.E0(Or_out), .E1(nor_1_out), .escolha(Sel_1), .S(MUX1_s));
  Mux_2x1 MUX3 (.E0(MUX1_s), .E1(MUX2_s), .escolha(Sel_0), .S(S));
  Mux_2x1 MUX2 (.E0(NAND_out), .E1(And_out), .escolha(Sel_1), .S(MUX2_s));

  // Notes on the sheet:
  //   0.0 = Or
  //   0.1 = And
  //   1.0 = Nor
  //   1.1 = Nand
endmodule

module Mux_4x1 (
  input  _3,
  input  _2,
  input  _1,
  input  _0,
  input  S1,
  input  S0,
  output Resposta
);

  wire _00_out, _01_out, _10_out, _11_out, not_1_out, not_2_out, not_3_out, not_4_out;

  not not_1 (not_1_out, S1);
  and _00 (_00_out, not_1_out, not_2_out, _0);
  not not_2 (not_2_out, S0);
  not not_3 (not_3_out, S1);
  and _01 (_01_out, not_3_out, S0, _1);
  and _10 (_10_out, S1, not_4_out, _2);
  not not_4 (not_4_out, S0);
  and _11 (_11_out, S1, S0, _3);
  or Or (Resposta, _00_out, _01_out, _10_out, _11_out);
endmodule

module Xor_Xnor_Or_Nor_com_Mux (
  input  E1,
  input  E0,
  input  S1,
  input  S0,
  output S
);

  wire _0_0_out, _0_1_out, _1_0_out, _1_1_out;

  xor _0_0 (_0_0_out, E0, E1);
  or _1_0 (_1_0_out, E0, E1);
  nor _1_1 (_1_1_out, E0, E1);
  xnor _0_1 (_0_1_out, E0, E1);
  Mux_4x1 mux_4x1_1 (.S1(S1), .S0(S0), ._3(_1_1_out), ._2(_1_0_out), ._1(_0_1_out), ._0(_0_0_out), .Resposta(S));

  // Notes on the sheet:
  //   S1/S0
  //   0.0 = XOR
  //   1.0 = OR
  //   1.1 = NOR
  //   0.1 = XNOR
endmodule

module Mux_8x1 (
  input  [2:0] Seletor,
  input  [7:0] Entradas,
  output Saida
);

  wire _0_out, _1_out, _2_out, _3_out, _4_out, _5_out, _6_out, _7_out, not_1_out, not_2_out, not_3_out,
       not_4_out, not_5_out, not_6_out, not_7_out, not_8_out, not_9_out, not_10_out, not_11_out, not_12_out;

  not not_1 (not_1_out, Seletor[2]);
  not not_2 (not_2_out, Seletor[1]);
  and _0 (_0_out, not_1_out, not_2_out, not_3_out, Entradas[0]);
  not not_3 (not_3_out, Seletor[0]);
  not not_4 (not_4_out, Seletor[2]);
  not not_5 (not_5_out, Seletor[1]);
  and _1 (_1_out, not_4_out, not_5_out, Seletor[0], Entradas[1]);
  not not_6 (not_6_out, Seletor[2]);
  and _2 (_2_out, not_6_out, Seletor[1], not_7_out, Entradas[2]);
  not not_7 (not_7_out, Seletor[0]);
  not not_8 (not_8_out, Seletor[2]);
  and _3 (_3_out, not_8_out, Seletor[1], Seletor[0], Entradas[3]);
  not not_9 (not_9_out, Seletor[1]);
  and _4 (_4_out, Seletor[2], not_9_out, not_10_out, Entradas[4]);
  not not_10 (not_10_out, Seletor[0]);
  not not_11 (not_11_out, Seletor[1]);
  and _5 (_5_out, Seletor[2], not_11_out, Seletor[0], Entradas[5]);
  and _6 (_6_out, Seletor[2], Seletor[1], not_12_out, Entradas[6]);
  not not_12 (not_12_out, Seletor[0]);
  and _7 (_7_out, Seletor[2], Seletor[1], Seletor[0], Entradas[7]);
  or Or (Saida, _0_out, _1_out, _2_out, _3_out, _4_out, _5_out, _6_out, _7_out);
endmodule

module Full_LU (
  input  E0,
  input  E1,
  input  S2,
  input  S1,
  input  S0,
  output Saida
);

  wire [7:0] _0_out;

  not _0 (_0_out[0], E0);
  not _1 (_0_out[1], E1);
  and _2 (_0_out[2], E0, E1);
  or _3 (_0_out[3], E0, E1);
  nand _4 (_0_out[4], E0, E1);
  nor _5 (_0_out[5], E0, E1);
  xor _6 (_0_out[6], E0, E1);
  xnor _7 (_0_out[7], E0, E1);
  Mux_8x1 MUX (.Entradas(_0_out), .Seletor({S2, S1, S0}), .Saida(Saida));
endmodule
