// Logisim project Projeto de unidades logicas e aritmeticas.circ as structural Verilog: 14 circuits, main circuit Half-sum
module Half_sum (
  input  a,
  input  b,
  output S1,
  output S0
);

  wire and_1_out, and_2_out, not_1_out, not_2_out;

  not not_1 (not_1_out, a);
  not not_2 (not_2_out, b);
  and and_1 (and_1_out, not_1_out, b);
  and and_2 (and_2_out, not_2_out, a);
  and and_3 (S1, a, b);
  or or_1 (S0, and_1_out, and_2_out);
endmodule

module Full_adder (
  input  a,
  input  b,
  input  c,
  output S0,
  output S1
);

  wire and_1_out, and_2_out, and_3_out, and_4_out, and_5_out, and_6_out, and_7_out, not_1_out, not_2_out,
       not_3_out, not_4_out, not_5_out, not_6_out;

  not not_1 (not_1_out, a);
  not not_2 (not_2_out, b);
  not not_3 (not_3_out, b);
  not not_4 (not_4_out, c);
  and and_1 (and_1_out, not_1_out, not_3_out, c);
  and and_2 (and_2_out, a, not_2_out, not_4_out);
  or or_1 (S0, and_2_out, and_1_out, and_4_out, and_3_out);
  not not_5 (not_5_out, c);
  not not_6 (not_6_out, a);
  and and_3 (and_3_out, a, b, c);
  and and_4 (and_4_out, not_6_out, b, not_5_out);
  and and_5 (and_5_out, b, c);
  and and_6 (and_6_out, a, c);
  or or_2 (S1, and_5_out, and_6_out, and_7_out);
  and and_7 (and_7_out, b, a);
endmodule

module Full_adder_com_half_sum (
  input  in_1,
  input  in_2,
  input  in_3,
  output out_4,
  output out_5
);

  wire half_sum_1_s0, half_sum_1_s1, half_sum_2_s1;

  Half_sum half_sum_1 (.a(in_1), .b(in_2), .S1(half_sum_1_s1), .S0(half_sum_1_s0));
  Half_sum half_sum_2 (.a(half_sum_1_s0), .b(in_3), .S1(half_sum_2_s1), .S0(out_5));
  Half_sum half_sum_3 (.a(half_sum_1_s1), .b(half_sum_2_s1), .S0(out_4));  // open: S1
endmodule

module Half_Sub (
  input  a,
  input  b,
  output sinal,
  output amplitude
);

  wire and_2_out, not_1_out, not_2_out;

  not not_1 (not_1_out, a);
  not not_2 (not_2_out, b);
  and and_1 (sinal, not_1_out, b);
  and and_2 (and_2_out, a, not_2_out);
  or or_1 (amplitude, sinal, and_2_out);
endmodule

module Full_sub (
  input  a,
  input  b,
  input  c,
  output sinal,
  output amplitude
);

  wire half_sub_1_amplitude, half_sub_1_sinal, half_sub_2_sinal;

  Half_Sub half_sub_1 (.a(a), .b(b), .sinal(half_sub_1_sinal), .amplitude(half_sub_1_amplitude));
  Half_Sub half_sub_2 (.a(half_sub_1_amplitude), .b(c), .sinal(half_sub_2_sinal), .amplitude(amplitude));
  or or_1 (sinal, half_sub_1_sinal, half_sub_2_sinal);
endmodule

module Full_adder_4_bits (
  input  a,
  input  b,
  input  c,
  input  d,
  output s2,
  output s1,
  output s0
);

  wire Full_adder_out_4, Full_adder_out_5, HA_s1;

  Full_adder_com_half_sum Full_adder (.in_1(a), .in_2(b), .in_3(c), .out_4(Full_adder_out_4), .out_5(Full_adder_out_5));
  Half_sum HA (.a(Full_adder_out_5), .b(d), .S1(HA_s1), .S0(s0));
  Half_sum HA_2 (.a(Full_adder_out_4), .b(HA_s1), .S1(s2), .S0(s1));
endmodule

module Full_sub_4_bits (
  input  a,
  input  b,
  input  c,
  input  d,
  output s2,
  output s1,
  output s0
);

  Full_sub Full_sub (.a(a), .b(b), .c(c), .sinal(s2), .amplitude(s1));
  Half_Sub Half_sub (.a(s1), .b(d), .amplitude(s0));  // open: sinal
endmodule

module FULL_ADDER_ENTRADA_5bits (
  input  [4:0] a,
  input  [4:0] b,
  output Carry_in,
  output [4:0] s
);

  wire full_adder_com_half_sum_1_out_4, full_adder_com_half_sum_2_out_4, full_adder_com_half_sum_4_out_4,
       half_sum_1_s1;

  Half_sum half_sum_1 (.a(b[0]), .b(a[0]), .S1(half_sum_1_s1), .S0(s[0]));
  Full_adder_com_half_sum full_adder_com_half_sum_1 (
    .in_1(a[2]), .in_2(b[2]), .in_3(full_adder_com_half_sum_2_out_4),
    .out_4(full_adder_com_half_sum_1_out_4), .out_5(s[2]));
  Full_adder_com_half_sum full_adder_com_half_sum_2 (
    .in_1(b[1]), .in_2(a[1]), .in_3(half_sum_1_s1), .out_4(full_adder_com_half_sum_2_out_4), .out_5(s[1]));
  Full_adder_com_half_sum full_adder_com_half_sum_3 (
    .in_1(a[4]), .in_2(b[4]), .in_3(full_adder_com_half_sum_4_out_4), .out_4(Carry_in), .out_5(s[4]));
  Full_adder_com_half_sum full_adder_com_half_sum_4 (
    .in_1(a[3]), .in_2(b[3]), .in_3(full_adder_com_half_sum_1_out_4),
    .out_4(full_adder_com_half_sum_4_out_4), .out_5(s[3]));
endmodule

module FULL_SUB_ENTRADA_5_bits (
  input  [4:0] a,
  input  [4:0] b,
  output Sinal,
  output [4:0] s
);

  wire full_sub_1_sinal, full_sub_2_sinal, full_sub_4_sinal, half_sub_1_sinal;

  Half_Sub half_sub_1 (.a(a[0]), .b(b[0]), .sinal(half_sub_1_sinal), .amplitude(s[0]));
  Full_sub full_sub_1 (.a(a[2]), .b(b[2]), .c(full_sub_2_sinal), .sinal(full_sub_1_sinal), .amplitude(s[2]));
  Full_sub full_sub_2 (.a(a[1]), .b(b[1]), .c(half_sub_1_sinal), .sinal(full_sub_2_sinal), .amplitude(s[1]));
  Full_sub full_sub_3 (.a(a[4]), .b(b[4]), .c(full_sub_4_sinal), .sinal(Sinal), .amplitude(s[4]));
  Full_sub full_sub_4 (.a(a[3]), .b(b[3]), .c(full_sub_1_sinal), .sinal(full_sub_4_sinal), .amplitude(s[3]));
endmodule

module IGUALDADE (
  input  [4:0] in_1,
  input  [4:0] in_2,
  output out_3
);

  wire full_sub_entrada_5_bits_1_sinal, or_1_out;
  wire [4:0] full_sub_entrada_5_bits_1_s;

  FULL_SUB_ENTRADA_5_bits full_sub_entrada_5_bits_1 (
    .a(in_1), .b(in_2), .Sinal(full_sub_entrada_5_bits_1_sinal), .s(full_sub_entrada_5_bits_1_s));
  not not_1 (out_3, or_1_out);
  or or_1 (or_1_out, full_sub_entrada_5_bits_1_sinal, full_sub_entrada_5_bits_1_s[0], full_sub_entrada_5_bits_1_s[1], full_sub_entrada_5_bits_1_s[2], full_sub_entrada_5_bits_1_s[3], full_sub_entrada_5_bits_1_s[4]);

  // Notes on the sheet:
  //   0-Diferente
  //   1-Igual
endmodule

module DESIGUALDADE (
  input  [4:0] a,
  input  [4:0] b,
  output out_3,
  output out_4,
  output out_5
);

  wire full_sub_entrada_5_bits_1_sinal, not_2_out, or_1_out;
  wire [4:0] full_sub_entrada_5_bits_1_s;

  FULL_SUB_ENTRADA_5_bits full_sub_entrada_5_bits_1 (
    .a(a), .b(b), .Sinal(full_sub_entrada_5_bits_1_sinal), .s(full_sub_entrada_5_bits_1_s));
  and and_1 (out_3, full_sub_entrada_5_bits_1_sinal, or_1_out);
  or or_1 (or_1_out, full_sub_entrada_5_bits_1_sinal, full_sub_entrada_5_bits_1_s[0], full_sub_entrada_5_bits_1_s[1], full_sub_entrada_5_bits_1_s[2], full_sub_entrada_5_bits_1_s[3], full_sub_entrada_5_bits_1_s[4]);
  not not_1 (out_4, or_1_out);
  not not_2 (not_2_out, full_sub_entrada_5_bits_1_sinal);
  and and_2 (out_5, or_1_out, not_2_out);

  // Notes on the sheet:
  //   a_b Comparision
endmodule

module LU___igualdade_desigualdade_complemento_de_1_e_2 (
  input  [4:0] a,
  input  [4:0] b,
  output a_b,
  output a_b_2,
  output a_b_3,
  output [4:0] C1_de_a,
  output [4:0] C1_de_b,
  output [4:0] C2_de_a,
  output [4:0] C2_de_b
);

  DESIGUALDADE desigualdade_1 (.a(a), .b(b), .out_3(a_b), .out_4(a_b_2), .out_5(a_b_3));
  Complemento_de_1___5bits_entrada complemento_de_1_5bits_entrada_1 (.a(a), .Complemento(C1_de_a));
  Complemento_de_2___5_Bits_entrada complemento_de_2_5_bits_entrada_1 (.a(a), .Valor(C2_de_a));
  Complemento_de_1___5bits_entrada complemento_de_1_5bits_entrada_2 (.a(b), .Complemento(C1_de_b));
  Complemento_de_2___5_Bits_entrada complemento_de_2_5_bits_entrada_2 (.a(b), .Valor(C2_de_b));
endmodule

module Complemento_de_1___5bits_entrada (
  input  [4:0] a,
  output [4:0] Complemento
);

  assign Complemento = ~a;  // NOT_Gate not_1, 5 bits wide
endmodule

module Complemento_de_2___5_Bits_entrada (
  input  [4:0] a,
  output [4:0] Valor
);

  wire [4:0] C1_complemento;

  Complemento_de_1___5bits_entrada C1 (.a(a), .Complemento(C1_complemento));
  FULL_ADDER_ENTRADA_5bits FA (.a(C1_complemento), .b(5'b00001), .s(Valor));  // open: Carry_in
endmodule
